# Fritzing sketch Home v1 (saved by Fritzing 0.9.3b)
circuit board: 8cm x 4cm
breadboards: 1

parts:
  TRI1 = BTA Triac [package="TO220 [THT]"]
  TRI2 = BTA Triac [package="TO220 [THT]"]
  TRI3 = BTA Triac [package="TO220 [THT]"]
  TRI4 = BTA Triac [package="TO220 [THT]"]
  U1 = MOC3031-M [package=dil06]
  U2 = MOC3031-M [package=dil06]
  U3 = MOC3031-M [package=dil06]
  U4 = MOC3031-M [package=dil06]
  R1 = Resistor [tolerance=±5% resistance=220 package=THT]
  R2 = Resistor [tolerance=±5% resistance=220 package=THT]
  R3 = Resistor [tolerance=±5% resistance=220 package=THT]
  R4 = Resistor [tolerance=±5% resistance=220 package=THT]
  ESP8266 = NodeMCU V1.0
  R5 = Resistor [tolerance=±5% resistance=220 package=THT]
  R6 = Resistor [tolerance=±5% resistance=220 package=THT]
  R7 = Resistor [tolerance=±5% resistance=220 package=THT]
  R8 = Resistor [tolerance=±5% resistance=220 package=THT]
  J1 = Screw terminal - 2 pins [package=THT]
  J2 = Screw terminal - 2 pins [package=THT]
  J3 = Screw terminal - 2 pins [package=THT]

nets:
  N1: TRI1.A1, J2.pin1
  N2: TRI1.A2, TRI2.A2, TRI3.A2, TRI4.A2, R1.Pin_1, R2.Pin_1, R3.Pin_1, R4.Pin_1, J1.pin1
  N3: TRI1.G, U1.4
  N4: TRI2.A1, J2.pin2
  N5: TRI2.G, U2.4
  N6: TRI3.A1, J3.pin1
  N7: TRI3.G, U3.4
  N8: TRI4.A1, J3.pin2
  N9: TRI4.G, U4.4
  N10: U1.1, R6.Pin_1
  N11: U1.2, U2.2, U3.2, U4.2, ESP8266.GND
  N12: U1.6, R4.Pin_0
  N13: U2.1, R8.Pin_1
  N14: U2.6, R1.Pin_0
  N15: U3.1, R7.Pin_1
  N16: U3.6, R2.Pin_0
  N17: U4.1, R5.Pin_1
  N18: U4.6, R3.Pin_0
  N19: ESP8266.D5, R6.Pin_0
  N20: ESP8266.D6, R8.Pin_0
  N21: ESP8266.D7, R7.Pin_0
  N22: ESP8266.D8, R5.Pin_0

notes:
  TABVN
  NODEMCU V1.0
  L
  N
  L1
  L2
  L3
  L4

custom parts:
  BTA Triac: BTA16
  NodeMCU V1.0: ESP8266 based NodeMCU
